# Fritzing sketch light-diagram (saved by Fritzing 0.9.3b)

parts:
  Part1 = Arduino Uno (Rev3)
  Part2 = Adafruit Breadboard-Friendly NeoPixel [part_number="Adafruit #1312"]
  Part3 = Adafruit Breadboard-Friendly NeoPixel [part_number="Adafruit #1312"]
  Part4 = Adafruit Breadboard-Friendly NeoPixel [part_number="Adafruit #1312"]

nets:
  N1: Part1.D9_PWM, Part2.IN
  VDD: Part1.5V, Part2.VDD, Part3.VDD, Part4.VDD
  GND: Part1.GND, Part2.GND, Part3.GND, Part4.GND
  N2: Part2.OUT, Part3.IN
  N3: Part3.OUT, Part4.IN

custom parts:
  Adafruit Breadboard-Friendly NeoPixel: This is the easiest way possible to add small, bright RGB pixels to your project. We took the same technology from our Flora NeoPixels and made them breadboard friendly, with two rows of 3 x 0.1" spaced header on each side for easy soldering, chaining and breadboarding. These ultra-bright LEDs have a constant-current driver cooked right into the LED package! The pixels are chainable - so you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
