# Fritzing sketch reinduino-diagram (saved by Fritzing 0.9.3b)
breadboards: 1

parts:
  Part1 = Arduino Uno (Rev3)
  Part2 = Adafruit Breadboard-Friendly NeoPixel [part_number="Adafruit #1312"]
  J2 = Piezo Speaker
  J3 = Basic Servo

nets:
  N1: Part1.D9_PWM, J2.pin2
  N2: Part1.D10_PWM/SS, J3.pulse
  GND: Part1.GND, Part2.GND, J2.pin1, J3.gnd
  N3: Part1.D6_PWM, Part2.IN
  5V: Part1.5V, Part2.VDD, J3.vcc

custom parts:
  Adafruit Breadboard-Friendly NeoPixel: This is the easiest way possible to add small, bright RGB pixels to your project. We took the same technology from our Flora NeoPixels and made them breadboard friendly, with two rows of 3 x 0.1" spaced header on each side for easy soldering, chaining and breadboarding. These ultra-bright LEDs have a constant-current driver cooked right into the LED package! The pixels are chainable - so you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
